// Logisim project 8BCPU.circ as structural Verilog: 6 circuits, main circuit main
module main (
  input  in_1,
  input  [7:0] Testing_Data,
  input  [3:0] OE_Testing_Data,
  input  OE_Testing_Data_2,
  input  WE,
  input  OE,
  input  Counter_OE,
  input  Internal_OE,
  input  Counter_Enable,
  input  WE_2,
  input  OE_2,
  input  WE_3,
  input  WE_4,
  input  OE_3,
  input  OE_4,
  input  WE_5,
  input  WE_6,
  input  OE_5,
  input  OE_6,
  input  WE_7,
  output [3:0] MAR_Content,
  output [3:0] Counter_Content,
  output [7:0] IR_Content,
  output [7:0] MBR_Content,
  output [7:0] out_25,
  output [7:0] Reg_A_Content,
  output [7:0] ALU_Result,
  output [7:0] Reg_B_Content
);

  wire CLK_out;
  wire [3:0] controlled_buffer_1_out, MAR_dout;
  wire [7:0] ALU_dout, bit_extender_1_out, Instruction_Register_dout;
  wire [31:0] decimal_decorder_1_dout, decimal_decorder_2_dout, decimal_decorder_3_dout,
       decimal_decorder_4_dout;

  Clock CLK (.out(CLK_out));
  assign controlled_buffer_1_out = Counter_OE ? Counter_Content : 4'bz;  // Controlled_Buffer controlled_buffer_1
  Counter #(.width(4), .max('h3)) Program_Counter (
    .D(controlled_buffer_1_out), .count(Counter_Enable), .Q(Counter_Content), .clk(CLK_out));  // open: load, carry, clr
  Register Instruction_Register (
    .CLK(CLK_out), .WE(WE_3), .OE(OE_4), .Din(ALU_dout), .Dout(Instruction_Register_dout),
    .Stored_Data(IR_Content));
  Register Register_A (.CLK(CLK_out), .WE(WE_5), .Din(ALU_dout), .Stored_Data(Reg_A_Content));  // open: OE, Dout
  ALU ALU (
    .Reg_A(Reg_A_Content), .Reg_B(Reg_B_Content), .OE(OE_6), .ALU_Result(ALU_Result), .Dout(ALU_dout));  // open: Carry_Output
  Register Register_B (.CLK(CLK_out), .WE(WE_7), .Din(ALU_dout), .Stored_Data(Reg_B_Content));  // open: OE, Dout
  assign bit_extender_1_out = {{4{1'b0}}, Counter_Content};  // Bit_Extender bit_extender_1
  Decimal_Decorder decimal_decorder_1 (.Din(Reg_A_Content), .Dout(decimal_decorder_1_dout));
  Decimal_Decorder decimal_decorder_2 (.Din(Reg_B_Content), .Dout(decimal_decorder_2_dout));
  _7_Segment_Display u_7_segment_display_1 (
    .g(decimal_decorder_3_dout[3]), .f(decimal_decorder_3_dout[2]), .a(decimal_decorder_3_dout[1]),
    .b(decimal_decorder_3_dout[0]), .e(decimal_decorder_3_dout[19]), .d(decimal_decorder_3_dout[18]),
    .c(decimal_decorder_3_dout[17]), .dp(decimal_decorder_3_dout[16]));
  Decimal_Decorder decimal_decorder_3 (.Din(bit_extender_1_out), .Dout(decimal_decorder_3_dout));
  _7_Segment_Display u_7_segment_display_2 (
    .g(decimal_decorder_1_dout[15]), .f(decimal_decorder_1_dout[14]), .a(decimal_decorder_1_dout[13]),
    .b(decimal_decorder_1_dout[12]), .e(decimal_decorder_1_dout[31]), .d(decimal_decorder_1_dout[30]),
    .c(decimal_decorder_1_dout[29]), .dp(decimal_decorder_1_dout[28]));
  _7_Segment_Display u_7_segment_display_3 (
    .g(decimal_decorder_1_dout[11]), .f(decimal_decorder_1_dout[10]), .a(decimal_decorder_1_dout[9]),
    .b(decimal_decorder_1_dout[8]), .e(decimal_decorder_1_dout[27]), .d(decimal_decorder_1_dout[26]),
    .c(decimal_decorder_1_dout[25]), .dp(decimal_decorder_1_dout[24]));
  _7_Segment_Display u_7_segment_display_4 (
    .g(decimal_decorder_2_dout[15]), .f(decimal_decorder_2_dout[14]), .a(decimal_decorder_2_dout[13]),
    .b(decimal_decorder_2_dout[12]), .e(decimal_decorder_2_dout[31]), .d(decimal_decorder_2_dout[30]),
    .c(decimal_decorder_2_dout[29]), .dp(decimal_decorder_2_dout[28]));
  _7_Segment_Display u_7_segment_display_5 (
    .g(decimal_decorder_2_dout[11]), .f(decimal_decorder_2_dout[10]), .a(decimal_decorder_2_dout[9]),
    .b(decimal_decorder_2_dout[8]), .e(decimal_decorder_2_dout[27]), .d(decimal_decorder_2_dout[26]),
    .c(decimal_decorder_2_dout[25]), .dp(decimal_decorder_2_dout[24]));
  BitSelector #(.group(4)) bitselector_1 (.in(Instruction_Register_dout), .out(controlled_buffer_1_out), .sel(1'b0));
  _7_Segment_Display u_7_segment_display_6 (
    .g(decimal_decorder_1_dout[3]), .f(decimal_decorder_1_dout[2]), .a(decimal_decorder_1_dout[1]),
    .b(decimal_decorder_1_dout[0]), .e(decimal_decorder_1_dout[19]), .d(decimal_decorder_1_dout[18]),
    .c(decimal_decorder_1_dout[17]), .dp(decimal_decorder_1_dout[16]));
  _7_Segment_Display u_7_segment_display_7 (
    .g(decimal_decorder_1_dout[7]), .f(decimal_decorder_1_dout[6]), .a(decimal_decorder_1_dout[5]),
    .b(decimal_decorder_1_dout[4]), .e(decimal_decorder_1_dout[23]), .d(decimal_decorder_1_dout[22]),
    .c(decimal_decorder_1_dout[21]), .dp(decimal_decorder_1_dout[20]));
  _7_Segment_Display u_7_segment_display_8 (
    .g(decimal_decorder_2_dout[7]), .f(decimal_decorder_2_dout[6]), .a(decimal_decorder_2_dout[5]),
    .b(decimal_decorder_2_dout[4]), .e(decimal_decorder_2_dout[23]), .d(decimal_decorder_2_dout[22]),
    .c(decimal_decorder_2_dout[21]), .dp(decimal_decorder_2_dout[20]));
  _7_Segment_Display u_7_segment_display_9 (
    .g(decimal_decorder_2_dout[3]), .f(decimal_decorder_2_dout[2]), .a(decimal_decorder_2_dout[1]),
    .b(decimal_decorder_2_dout[0]), .e(decimal_decorder_2_dout[19]), .d(decimal_decorder_2_dout[18]),
    .c(decimal_decorder_2_dout[17]), .dp(decimal_decorder_2_dout[16]));
  assign ALU_dout = OE_Testing_Data_2 ? Testing_Data : 8'bz;  // Controlled_Buffer controlled_buffer_2
  LED D7 (.in(ALU_dout[7]));
  LED D6 (.in(ALU_dout[6]));
  LED D4 (.in(ALU_dout[4]));
  LED D2 (.in(ALU_dout[2]));
  LED D3 (.in(ALU_dout[3]));
  LED D5 (.in(ALU_dout[5]));
  LED D1 (.in(ALU_dout[1]));
  LED D0 (.in(ALU_dout[0]));
  MAR MAR (.CLK(CLK_out), .WE(WE), .OE(OE), .Din(controlled_buffer_1_out), .Dout(MAR_dout), .Stored_Data(MAR_Content));
  assign ALU_dout = Internal_OE ? MBR_Content : 8'bz;  // Controlled_Buffer controlled_buffer_3
  Register MBR (.CLK(CLK_out), .WE(WE_2), .OE(OE_2), .Din(ALU_dout), .Dout(ALU_dout), .Stored_Data(MBR_Content));
  Register Output_Register (.CLK(CLK_out), .WE(WE_6), .OE(OE_5), .Din(ALU_dout), .Dout(ALU_dout), .Stored_Data(out_25));
  assign MAR_dout = in_1 ? OE_Testing_Data : 4'bz;  // Controlled_Buffer controlled_buffer_4
  Decimal_Decorder decimal_decorder_4 (.Din(out_25), .Dout(decimal_decorder_4_dout));
  _7_Segment_Display u_7_segment_display_10 (
    .g(decimal_decorder_4_dout[11]), .f(decimal_decorder_4_dout[10]), .a(decimal_decorder_4_dout[9]),
    .b(decimal_decorder_4_dout[8]), .e(decimal_decorder_4_dout[27]), .d(decimal_decorder_4_dout[26]),
    .c(decimal_decorder_4_dout[25]), .dp(decimal_decorder_4_dout[24]));
  _7_Segment_Display u_7_segment_display_11 (
    .g(decimal_decorder_4_dout[15]), .f(decimal_decorder_4_dout[14]), .a(decimal_decorder_4_dout[13]),
    .b(decimal_decorder_4_dout[12]), .e(decimal_decorder_4_dout[31]), .d(decimal_decorder_4_dout[30]),
    .c(decimal_decorder_4_dout[29]), .dp(decimal_decorder_4_dout[28]));
  _7_Segment_Display u_7_segment_display_12 (
    .g(decimal_decorder_4_dout[7]), .f(decimal_decorder_4_dout[6]), .a(decimal_decorder_4_dout[5]),
    .b(decimal_decorder_4_dout[4]), .e(decimal_decorder_4_dout[23]), .d(decimal_decorder_4_dout[22]),
    .c(decimal_decorder_4_dout[21]), .dp(decimal_decorder_4_dout[20]));
  _7_Segment_Display u_7_segment_display_13 (
    .g(decimal_decorder_4_dout[3]), .f(decimal_decorder_4_dout[2]), .a(decimal_decorder_4_dout[1]),
    .b(decimal_decorder_4_dout[0]), .e(decimal_decorder_4_dout[19]), .d(decimal_decorder_4_dout[18]),
    .c(decimal_decorder_4_dout[17]), .dp(decimal_decorder_4_dout[16]));
  LED D6_2 (.in(ALU_dout[6]));
  LED D4_2 (.in(ALU_dout[4]));
  LED D7_2 (.in(ALU_dout[7]));
  LED D5_2 (.in(ALU_dout[5]));
  LED D3_2 (.in(ALU_dout[3]));
  LED D2_2 (.in(ALU_dout[2]));
  LED D1_2 (.in(ALU_dout[1]));
  LED D0_2 (.in(ALU_dout[0]));
  RAM #(.addrWidth(4), .bus("separate")) ram_1 (
    .addr(MAR_dout), .din(ALU_dout), .data(ALU_dout), .str(WE_4), .clk(CLK_out), .ld(OE_3));  // open: sel, clr

  // Notes on the sheet:
  //   Internal Address Bus (4 bits)
  //   Internal Data Bus
  //   External Address Bus
  //   External Data Bus
endmodule

module Memory (
  input  CLK,
  input  WE,
  input  Din,
  input  OE,
  input  RESET,
  output Dout,
  output Stored_Data
);

  wire and_1_out, and_2_out, not_1_out, or_1_out;

  not not_1 (not_1_out, WE);
  and and_1 (and_1_out, Stored_Data, not_1_out);
  and and_2 (and_2_out, WE, Din);
  or or_1 (or_1_out, and_1_out, and_2_out);
  D_Flip_Flop d_ff_1 (.clk(CLK), .D(or_1_out), .Q(Stored_Data), .reset(RESET));  // open: Qn, preset, en
  assign Dout = OE ? Stored_Data : 1'bz;  // Controlled_Buffer controlled_buffer_1

  // Notes on the sheet:
  //   Memory Cell
endmodule

module Register (
  input  CLK,
  input  WE,
  input  OE,
  input  [7:0] Din,
  output [7:0] Dout,
  output [7:0] Stored_Data
);

  Memory _0 (.CLK(CLK), .WE(WE), .Din(Din[0]), .OE(OE), .Dout(Dout[0]), .Stored_Data(Stored_Data[0]));  // open: RESET
  Memory _1 (.CLK(CLK), .WE(WE), .Din(Din[1]), .OE(OE), .Dout(Dout[1]), .Stored_Data(Stored_Data[1]));  // open: RESET
  Memory _2 (.CLK(CLK), .WE(WE), .Din(Din[2]), .OE(OE), .Dout(Dout[2]), .Stored_Data(Stored_Data[2]));  // open: RESET
  Memory _3 (.CLK(CLK), .WE(WE), .Din(Din[3]), .OE(OE), .Dout(Dout[3]), .Stored_Data(Stored_Data[3]));  // open: RESET
  Memory _4 (.CLK(CLK), .WE(WE), .Din(Din[4]), .OE(OE), .Dout(Dout[4]), .Stored_Data(Stored_Data[4]));  // open: RESET
  Memory _5 (.CLK(CLK), .WE(WE), .Din(Din[5]), .OE(OE), .Dout(Dout[5]), .Stored_Data(Stored_Data[5]));  // open: RESET
  Memory _6 (.CLK(CLK), .WE(WE), .Din(Din[6]), .OE(OE), .Dout(Dout[6]), .Stored_Data(Stored_Data[6]));  // open: RESET
  Memory _7 (.CLK(CLK), .WE(WE), .Din(Din[7]), .OE(OE), .Dout(Dout[7]), .Stored_Data(Stored_Data[7]));  // open: RESET

  // Notes on the sheet:
  //   Memory Register
endmodule

module MAR (
  input  CLK,
  input  WE,
  input  OE,
  input  [3:0] Din,
  output [3:0] Dout,
  output [3:0] Stored_Data
);

  Memory _0 (.CLK(CLK), .WE(WE), .Din(Din[0]), .OE(OE), .Dout(Dout[0]), .Stored_Data(Stored_Data[0]));  // open: RESET
  Memory _1 (.CLK(CLK), .WE(WE), .Din(Din[1]), .OE(OE), .Dout(Dout[1]), .Stored_Data(Stored_Data[1]));  // open: RESET
  Memory _2 (.CLK(CLK), .WE(WE), .Din(Din[2]), .OE(OE), .Dout(Dout[2]), .Stored_Data(Stored_Data[2]));  // open: RESET
  Memory _3 (.CLK(CLK), .WE(WE), .Din(Din[3]), .OE(OE), .Dout(Dout[3]), .Stored_Data(Stored_Data[3]));  // open: RESET

  // Notes on the sheet:
  //   MAR
endmodule

module ALU (
  input  [7:0] Reg_A,
  input  [7:0] Reg_B,
  input  OE,
  output [7:0] ALU_Result,
  output [7:0] Dout,
  output Carry_Output
);

  Adder adder_1 (.a(Reg_A), .b(Reg_B), .out(ALU_Result), .cout(Carry_Output));  // open: cin
  assign Dout = OE ? ALU_Result : 8'bz;  // Controlled_Buffer controlled_buffer_1

  // Notes on the sheet:
  //   ALU (8 bits)
endmodule

// DD
module Decimal_Decorder (
  input  [7:0] Din,
  output [31:0] Dout
);

  ROM #(.dataWidth(32)) rom_1 (
    .addr(Din),
    .data({Dout[31:28], Dout[15:12], Dout[27:24], Dout[11:8], Dout[23:20], Dout[7:4], Dout[19:16], Dout[3:0]}));  // open: sel

  // Notes on the sheet:
  //   contents of rom_1 (hex, n*v repeats v):
  //   e7 21 cb 6b 2d 6e ee 23 ef 2f 21e7 2121 21cb 216b 212d 216e 21ee 2123 21ef 212f cbe7 cb21 cbcb cb6b
  //   cb2d cb6e cbee cb23 cbef cb2f 6be7 6b21 6bcb 6b6b 6b2d 6b6e 6bee 6b23 6bef 6b2f 2de7 2d21 2dcb 2d6b
  //   2d2d 2d6e 2dee 2d23 2def 2d2f 6ee7 6e21 6ecb 6e6b 6e2d 6e6e 6eee 6e23 6eef 6e2f eee7 ee21 eecb ee6b
  //   ee2d ee6e eeee ee23 eeef ee2f 23e7 2321 23cb 236b 232d 236e 23ee 2323 23ef 232f efe7 ef21 efcb ef6b
  //   ef2d ef6e efee ef23 efef ef2f 2fe7 2f21 2fcb 2f6b 2f2d 2f6e 2fee 2f23 2fef 2f2f 21e7e7 21e721 21e7cb
  //   21e76b 21e72d 21e76e 21e7ee 21e723 21e7ef 21e72f 2121e7 212121 2121cb 21216b 21212d 21216e 2121ee
  //   212123 2121ef 21212f 21cbe7 21cb21 21cbcb 21cb6b 21cb2d 21cb6e 21cbee 21cb23 21cbef 21cb2f 216be7
  //   216b21 216bcb 216b6b 216b2d 216b6e 216bee 216b23 216bef 216b2f 212de7 212d21 212dcb 212d6b 212d2d
  //   212d6e 212dee 212d23 212def 212d2f 216ee7 216e21 216ecb 216e6b 216e2d 216e6e 216eee 216e23 216eef
  //   216e2f 21eee7 21ee21 21eecb 21ee6b 21ee2d 21ee6e 21eeee 21ee23 21eeef 21ee2f 2123e7 212321 2123cb
  //   21236b 21232d 21236e 2123ee 212323 2123ef 21232f 21efe7 21ef21 21efcb 21ef6b 21ef2d 21ef6e 21efee
  //   21ef23 21efef 21ef2f 212fe7 212f21 212fcb 212f6b 212f2d 212f6e 212fee 212f23 212fef 212f2f cbe7e7
  //   cbe721 cbe7cb cbe76b cbe72d cbe76e cbe7ee cbe723 cbe7ef cbe72f cb21e7 cb2121 cb21cb cb216b cb212d
  //   cb216e cb21ee cb2123 cb21ef cb212f cbcbe7 cbcb21 cbcbcb cbcb6b cbcb2d cbcb6e cbcbee cbcb23 cbcbef
  //   cbcb2f cb6be7 cb6b21 cb6bcb cb6b6b cb6b2d cb6b6e cb6bee cb6b23 cb6bef cb6b2f cb2de7 cb2d21 cb2dcb
  //   cb2d6b cb2d2d cb2d6e cb2dee cb2d23 cb2def cb2d2f cb6ee7 cb6e21 cb6ecb cb6e6b cb6e2d cb6e6e
endmodule
